// Logisim project File-Reg.circ as structural Verilog: 1 circuit, main circuit main
// File-Reg
module main (
  input  [31:0] WriteData,
  input  Clear,
  input  Write,
  input  [4:0] INPUT_Address,
  input  [4:0] Out_Address_1,
  input  [4:0] Out_Address_2,
  input  in_7,
  input  [3:0] in_8,
  output [31:0] Output1_OP_1,
  output [31:0] Output2_OP_2,
  output [31:0] out_11
);

  wire clock_1_out, demultiplexer_1_out0, demultiplexer_1_out1, demultiplexer_1_out2, demultiplexer_1_out3,
       demultiplexer_1_out4, demultiplexer_1_out5, demultiplexer_1_out6, demultiplexer_1_out7;
  wire [7:0] _1, _2, _3;
  wire [31:0] and_1_out, divider_1_out, multiplier_1_out, nand_1_out, nor_1_out, not_1_out, or_1_out,
       register_1_q, register_2_q, register_3_q, register_4_q, register_5_q, register_6_q, register_7_q,
       register_8_q, register_9_q, register_10_q, register_11_q, register_12_q, register_13_q, register_14_q,
       register_15_q, register_16_q, register_17_q, register_18_q, register_19_q, register_20_q,
       register_21_q, register_22_q, register_23_q, register_24_q, register_25_q, register_26_q,
       register_27_q, register_28_q, register_29_q, register_30_q, register_31_q, register_32_q, xor_1_out;

  Demultiplexer #(.select(5), .enable("false")) demultiplexer_1 (
    .out0(demultiplexer_1_out0), .out1(demultiplexer_1_out1), .out2(demultiplexer_1_out2),
    .out3(demultiplexer_1_out3), .out4(demultiplexer_1_out4), .out5(demultiplexer_1_out5),
    .out6(demultiplexer_1_out6), .out7(demultiplexer_1_out7), .out8(_1[0]), .out9(_1[1]), .out10(_1[2]),
    .out11(_1[3]), .out12(_1[4]), .out13(_1[5]), .out14(_1[6]), .out15(_1[7]), .out16(_2[0]), .out17(_2[1]),
    .out18(_2[2]), .out19(_2[3]), .out20(_2[4]), .out21(_2[5]), .out22(_2[6]), .out23(_2[7]), .out24(_3[0]),
    .out25(_3[1]), .out26(_3[2]), .out27(_3[3]), .out28(_3[4]), .out29(_3[5]), .out30(_3[6]), .out31(_3[7]),
    .in(Write), .sel(INPUT_Address));
  Clock clock_1 (.out(clock_1_out));
  Register #(.width(32)) register_1 (
    .D(WriteData), .en(demultiplexer_1_out0), .Q(register_1_q), .clk(clock_1_out), .clr(Clear));
  Register #(.width(32)) register_2 (
    .D(WriteData), .en(demultiplexer_1_out1), .Q(register_2_q), .clk(clock_1_out), .clr(Clear));
  Register #(.width(32)) register_3 (
    .D(WriteData), .en(demultiplexer_1_out2), .Q(register_3_q), .clk(clock_1_out), .clr(Clear));
  Register #(.width(32)) register_4 (
    .D(WriteData), .en(demultiplexer_1_out3), .Q(register_4_q), .clk(clock_1_out), .clr(Clear));
  Register #(.width(32)) register_5 (.D(WriteData), .Q(register_5_q), .clk(clock_1_out), .clr(Clear));  // open: en
  Register #(.width(32)) register_6 (
    .D(WriteData), .en(demultiplexer_1_out5), .Q(register_6_q), .clk(clock_1_out), .clr(Clear));
  Register #(.width(32)) register_7 (
    .D(WriteData), .en(demultiplexer_1_out6), .Q(register_7_q), .clk(clock_1_out), .clr(Clear));
  Register #(.width(32)) register_8 (
    .D(WriteData), .en(demultiplexer_1_out7), .Q(register_8_q), .clk(clock_1_out), .clr(Clear));
  assign not_1_out = ~Output2_OP_2;  // NOT_Gate not_1, 32 bits wide
  assign and_1_out = Output2_OP_2 & Output1_OP_1;  // AND_Gate and_1, 32 bits wide
  assign or_1_out = Output2_OP_2 | Output1_OP_1;  // OR_Gate or_1, 32 bits wide
  assign nand_1_out = ~(Output2_OP_2 & Output1_OP_1);  // NAND_Gate nand_1, 32 bits wide
  assign nor_1_out = ~(Output2_OP_2 | Output1_OP_1);  // NOR_Gate nor_1, 32 bits wide
  assign xor_1_out = Output2_OP_2 ^ Output1_OP_1;  // XOR_Gate xor_1, 32 bits wide
  Multiplier #(.width(32)) multiplier_1 (
    .a(Output2_OP_2), .b(Output1_OP_1), .out(multiplier_1_out));  // open: cin, cout
  Divider #(.width(32)) divider_1 (.a(Output2_OP_2), .b(Output1_OP_1), .out(divider_1_out));  // open: upper, rem
  Register #(.width(32)) register_9 (.D(WriteData), .en(_1[0]), .Q(register_9_q), .clk(clock_1_out), .clr(Clear));
  Register #(.width(32)) register_10 (.D(WriteData), .en(_1[1]), .Q(register_10_q), .clk(clock_1_out), .clr(Clear));
  Register #(.width(32)) register_11 (.D(WriteData), .en(_1[2]), .Q(register_11_q), .clk(clock_1_out), .clr(Clear));
  Register #(.width(32)) register_12 (.D(WriteData), .en(_1[3]), .Q(register_12_q), .clk(clock_1_out), .clr(Clear));
  Register #(.width(32)) register_13 (.D(WriteData), .en(_1[4]), .Q(register_13_q), .clk(clock_1_out), .clr(Clear));
  Register #(.width(32)) register_14 (.D(WriteData), .en(_1[5]), .Q(register_14_q), .clk(clock_1_out), .clr(Clear));
  Register #(.width(32)) register_15 (.D(WriteData), .en(_1[6]), .Q(register_15_q), .clk(clock_1_out), .clr(Clear));
  Register #(.width(32)) register_16 (.D(WriteData), .en(_1[7]), .Q(register_16_q), .clk(clock_1_out), .clr(Clear));
  Multiplexer #(.select(4), .width(32)) multiplexer_1 (
    .in0(not_1_out), .in1(and_1_out), .in2(or_1_out), .in3(nand_1_out), .in4(nor_1_out), .in5(xor_1_out),
    .in6(multiplier_1_out), .in7(divider_1_out), .out(out_11), .sel(in_8));  // open: in8, in9, in10, in11, in12, in13, in14, in15, en
  Register #(.width(32)) register_17 (.D(WriteData), .en(_2[0]), .Q(register_17_q), .clk(clock_1_out), .clr(Clear));
  Register #(.width(32)) register_18 (.D(WriteData), .en(_2[1]), .Q(register_18_q), .clk(clock_1_out), .clr(Clear));
  Register #(.width(32)) register_19 (.D(WriteData), .en(_2[2]), .Q(register_19_q), .clk(clock_1_out), .clr(Clear));
  Register #(.width(32)) register_20 (.D(WriteData), .en(_2[3]), .Q(register_20_q), .clk(clock_1_out), .clr(Clear));
  Register #(.width(32)) register_21 (.D(WriteData), .en(_2[4]), .Q(register_21_q), .clk(clock_1_out), .clr(Clear));
  Register #(.width(32)) register_22 (.D(WriteData), .en(_2[5]), .Q(register_22_q), .clk(clock_1_out), .clr(Clear));
  Register #(.width(32)) register_23 (.D(WriteData), .en(_2[6]), .Q(register_23_q), .clk(clock_1_out), .clr(Clear));
  Register #(.width(32)) register_24 (.D(WriteData), .en(_2[7]), .Q(register_24_q), .clk(clock_1_out), .clr(Clear));
  Register #(.width(32)) register_25 (.D(WriteData), .en(_3[0]), .Q(register_25_q), .clk(clock_1_out), .clr(Clear));
  Register #(.width(32)) register_26 (.D(WriteData), .en(_3[1]), .Q(register_26_q), .clk(clock_1_out), .clr(Clear));
  Register #(.width(32)) register_27 (.D(WriteData), .en(_3[2]), .Q(register_27_q), .clk(clock_1_out), .clr(Clear));
  Register #(.width(32)) register_28 (.D(WriteData), .en(_3[3]), .Q(register_28_q), .clk(clock_1_out), .clr(Clear));
  Register #(.width(32)) register_29 (.D(WriteData), .en(_3[4]), .Q(register_29_q), .clk(clock_1_out), .clr(Clear));
  Register #(.width(32)) register_30 (.D(WriteData), .en(_3[5]), .Q(register_30_q), .clk(clock_1_out), .clr(Clear));
  Register #(.width(32)) register_31 (.D(WriteData), .en(_3[6]), .Q(register_31_q), .clk(clock_1_out), .clr(Clear));
  Register #(.width(32)) register_32 (.D(WriteData), .en(_3[7]), .Q(register_32_q), .clk(clock_1_out), .clr(Clear));
  Multiplexer #(.select(5), .width(32), .enable("false")) multiplexer_2 (
    .in0(register_1_q), .in1(register_2_q), .in2(register_3_q), .in3(register_4_q), .in4(register_5_q),
    .in5(register_6_q), .in6(register_7_q), .in7(register_8_q), .in8(register_9_q), .in9(register_10_q),
    .in10(register_11_q), .in11(register_12_q), .in12(register_13_q), .in13(register_14_q),
    .in14(register_15_q), .in15(register_16_q), .in16(register_24_q), .in17(register_23_q),
    .in18(register_22_q), .in19(register_21_q), .in20(register_20_q), .in21(register_19_q),
    .in22(register_18_q), .in23(register_17_q), .in24(register_32_q), .in25(register_31_q),
    .in26(register_30_q), .in27(register_29_q), .in28(register_28_q), .in29(register_27_q),
    .in30(register_26_q), .in31(register_25_q), .out(Output1_OP_1), .sel(Out_Address_1));
  Multiplexer #(.select(5), .width(32), .enable("false")) multiplexer_3 (
    .in0(register_1_q), .in1(register_2_q), .in2(register_3_q), .in3(register_4_q), .in4(register_5_q),
    .in5(register_6_q), .in6(register_7_q), .in7(register_8_q), .in8(register_9_q), .in9(register_10_q),
    .in10(register_11_q), .in11(register_12_q), .in12(register_13_q), .in13(register_14_q),
    .in14(register_15_q), .in15(register_16_q), .in16(register_24_q), .in17(register_23_q),
    .in18(register_22_q), .in19(register_21_q), .in20(register_20_q), .in21(register_19_q),
    .in22(register_18_q), .in23(register_17_q), .in24(register_32_q), .in25(register_31_q),
    .in26(register_30_q), .in27(register_29_q), .in28(register_28_q), .in29(register_27_q),
    .in30(register_26_q), .in31(register_25_q), .out(Output2_OP_2), .sel(Out_Address_2));
endmodule
